# Fritzing sketch SimulacionPCB (saved by Fritzing 0.9.3b)
perfboards: 1

parts:
  Componente1 = Arduino Nano (Rev3.0)
  R1 = Resistor [tolerance=±5% resistance=220 package="0603 [SMD]"]
  DISPLAY1 = Grove 4 Digit Display
  R2 = Resistor [tolerance=±5% resistance=220 package="0603 [SMD]"]  # not connected
  S2 = Pushbutton [package="[SMD]"]
  S3 = Pushbutton [package="[SMD]"]  # not connected
  Vcc = Screw terminal - 2 pins [package=THT]  # not connected
  M1 = DC Motor  # not connected
  S4 = Toggle Switch [package=THT]
  U1 = Voltage Regulator - 5V [package="TO220 [THT]"]

nets:
  N1: Componente1.D11/MOSI, DISPLAY1.DIO
  N2: Componente1.D12/MISO, DISPLAY1.CLK
  N3: R1.Pin_1, S2.Pin_1
  GND: DISPLAY1.GND, S4.L1, U1.GND
